// Logisim project EXMEM.circ as structural Verilog: 1 circuit, main circuit EX_MEM
module EX_MEM (
  input  Clock,
  input  [31:0] ResultIn,
  input  [31:0] AddressCacheIn,
  input  ZeroIn,
  input  BranchIn,
  input  RtypeIn,
  input  JumpIn,
  input  MemToRegIn,
  input  RegDstIn,
  input  RegWrEnIn,
  input  [3:0] MemWriteMaskIn,
  input  LBIn,
  input  [4:0] WrIdxIn,
  output [31:0] ResultOut,
  output [31:0] AddressCacheOut,
  output ZeroOut,
  output BranchOut,
  output RtypeOut,
  output JumpOut,
  output MemToRegOut,
  output RegDstOut,
  output RegWrEnOut,
  output [3:0] MemWriteMaskOut,
  output LBOut,
  output [4:0] WrIdxOut
);

  Register #(.width(32)) register_1 (.D(ResultIn), .clk(Clock), .Q(ResultOut));  // open: en, clr
  Register #(.width(1)) register_2 (.D(ZeroIn), .clk(Clock), .Q(ZeroOut));  // open: en, clr
  Register #(.width(1)) register_3 (.D(RtypeIn), .clk(Clock), .Q(RtypeOut));  // open: en, clr
  Register #(.width(1)) register_4 (.D(MemToRegIn), .clk(Clock), .Q(MemToRegOut));  // open: en, clr
  Register #(.width(1)) register_5 (.D(RegDstIn), .clk(Clock), .Q(RegDstOut));  // open: en, clr
  Register #(.width(1)) register_6 (.D(RegWrEnIn), .clk(Clock), .Q(RegWrEnOut));  // open: en, clr
  Register #(.width(4)) register_7 (.D(MemWriteMaskIn), .clk(Clock), .Q(MemWriteMaskOut));  // open: en, clr
  Register #(.width(1)) register_8 (.D(LBIn), .clk(Clock), .Q(LBOut));  // open: en, clr
  Register #(.width(5)) register_9 (.D(WrIdxIn), .clk(Clock), .Q(WrIdxOut));  // open: en, clr
  Register #(.width(32)) register_10 (.D(AddressCacheIn), .clk(Clock), .Q(AddressCacheOut));  // open: en, clr
  Register #(.width(1)) register_11 (.D(BranchIn), .clk(Clock), .Q(BranchOut));  // open: en, clr
  Register #(.width(1)) register_12 (.D(JumpIn), .clk(Clock), .Q(JumpOut));  // open: en, clr
endmodule
