// Logisim project alu.circ as structural Verilog: 1 circuit, main circuit ALU
module ALU (
  input  [31:0] ReadData1,
  input  [31:0] ReadData2,
  input  [4:0] ControlBits,
  output [31:0] Result,
  output Zero
);

  Multiplexer #(.enable("true"), .select(5), .width(32)) multiplexer_1 (
    .out(Result), .sel(ControlBits));  // open: in0, in1, in2, in3, in4, in5, in6, in7, in8, in9, in10, in11, in12, in13, in14, in15, in16, in17, in18, in19, in20, in21, in22, in23, in24, in25, in26, in27, in28, in29, in30, in31, en
endmodule
