// Logisim project branch_predictor.circ as structural Verilog: 1 circuit, main circuit branchPredictor
module branchPredictor (
  input  Jump,
  input  Branch,
  input  Clock,
  input  Zero,
  output Freeze,
  output Prediction
);

  wire and_1_out, and_2_out, and_3_out, and_4_out, and_5_out, and_6_out, comparator_1_gt, not_1_out,
       or_1_out, or_2_out, or_3_out, Q1, Q2;

  not not_1 (not_1_out, Q1);
  and and_1 (and_1_out, Q2, Zero);
  and and_2 (and_2_out, Zero, not_1_out);
  or or_1 (or_1_out, and_1_out, and_2_out, and_3_out);
  and and_3 (and_3_out, not_1_out, Q2);
  and and_4 (and_4_out, Q2, Q1);
  and and_5 (and_5_out, Q1, Zero);
  or or_2 (or_2_out, and_4_out, and_5_out, and_6_out);
  and and_6 (and_6_out, Q2, Zero);
  Register #(.width(1)) register_1 (.D(or_1_out), .clk(Clock), .Q(Q1));  // open: en, clr
  Register #(.width(1)) register_2 (.D(or_2_out), .clk(Clock), .Q(Q2));  // open: en, clr
  Counter #(.max('h3), .width(2)) counter_1 ();  // open: clr, load, up, count, clk, D, carry, Q
  Comparator #(.mode("unsigned"), .width(2)) comparator_1 (
    .a({Q2, Q1}), .b(2'b01), .gt(comparator_1_gt));  // open: eq, lt
  or or_3 (or_3_out, Jump, Branch);
  Multiplexer multiplexer_1 (.in0(1'b0), .in1(comparator_1_gt), .out(Prediction), .sel(or_3_out));
endmodule
