// Logisim project cache.circ as structural Verilog: 1 circuit, main circuit main
module main (
  input  Clock,
  input  [31:0] WriteData,
  input  [31:0] Address,
  input  in_4,
  output [31:0] ReadData,
  output HIT,
  output [31:0] AddressOut
);

  wire and_1_out, and_2_out, and_3_out, and_4_out, and_5_out, and_6_out, and_7_out, and_8_out, and_9_out,
       and_10_out, and_11_out, and_12_out, and_22_out, and_23_out, and_32_out, and_33_out, comparator_2_eq,
       comparator_4_eq, comparator_6_eq, comparator_8_eq, or_1_out, or_2_out, or_3_out, or_4_out, Select_0,
       Select_1, Select_2, Select_3, Set0, Set1, Set2, Set3, WE0, WE1, WE2, WE3, WE4, WE5, WE6, WE7, WE8,
       WE9, WE10, WE11, WE12, WE13, WE14, WE15, WE16, WE17, WE18, WE19, WE20, WE21, WE22, WE23, WE24, WE25,
       WE26, WE27, WE28, WE29, WE30, WE31, WH, Word0, Word1, Word2, Word3;
  wire [11:0] B0, B1, B2, B3, B4, B5, B6, B7;
  wire [31:0] multiplexer_1_out, multiplexer_2_out, multiplexer_3_out, multiplexer_4_out, multiplexer_5_out,
       multiplexer_6_out, multiplexer_7_out, multiplexer_8_out, multiplexer_9_out, multiplexer_10_out,
       multiplexer_11_out, multiplexer_12_out, W0, W1, W2, W3, W4, W5, W6, W7, W8, W9, W10, W11, W12, W13,
       W14, W15, W16, W17, W18, W19, W20, W21, W22, W23, W24, W25, W26, W27, W28, W29, W30, W31;

  Register #(.width(12)) register_1 (.Q(B0));  // open: D, en, clk, clr
  Register #(.width(12)) register_2 (.Q(B1));  // open: D, en, clk, clr
  Register #(.width(12)) register_3 (.Q(B2));  // open: D, en, clk, clr
  Register #(.width(12)) register_4 (.Q(B3));  // open: D, en, clk, clr
  Register #(.width(12)) register_5 (.Q(B4));  // open: D, en, clk, clr
  Register #(.width(12)) register_6 (.Q(B5));  // open: D, en, clk, clr
  Register #(.width(12)) register_7 (.Q(B6));  // open: D, en, clk, clr
  Register #(.width(12)) register_8 (.Q(B7));  // open: D, en, clk, clr
  Decoder #(.select(2)) decoder_1 (.out0(Set0), .out1(Set1), .out2(Set2), .out3(Set3), .sel(Address[5:4]));  // open: en
  Decoder #(.select(2)) decoder_2 (
    .out0(Word0), .out1(Word1), .out2(Word2), .out3(Word3), .sel(Address[3:2]));  // open: en
  Register #(.width(32)) register_9 (.D(WriteData), .en(WE0), .clk(Clock), .Q(W0));  // open: clr
  Register #(.width(32)) register_10 (.D(WriteData), .en(WE4), .clk(Clock), .Q(W4));  // open: clr
  Register #(.width(32)) register_11 (.D(WriteData), .en(WE8), .clk(Clock), .Q(W8));  // open: clr
  Register #(.width(32)) register_12 (.D(WriteData), .en(WE12), .clk(Clock), .Q(W12));  // open: clr
  Register #(.width(32)) register_13 (.D(WriteData), .en(WE16), .clk(Clock), .Q(W16));  // open: clr
  Register #(.width(32)) register_14 (.D(WriteData), .en(WE20), .clk(Clock), .Q(W20));  // open: clr
  Register #(.width(32)) register_15 (.D(WriteData), .en(WE24), .clk(Clock), .Q(W24));  // open: clr
  Register #(.width(32)) register_16 (.D(WriteData), .en(WE28), .clk(Clock), .Q(W28));  // open: clr
  Register #(.width(32)) register_17 (.D(WriteData), .en(WE1), .clk(Clock), .Q(W1));  // open: clr
  Register #(.width(32)) register_18 (.D(WriteData), .en(WE5), .clk(Clock), .Q(W5));  // open: clr
  Register #(.width(32)) register_19 (.D(WriteData), .en(WE9), .clk(Clock), .Q(W9));  // open: clr
  Register #(.width(32)) register_20 (.D(WriteData), .en(WE13), .clk(Clock), .Q(W13));  // open: clr
  Register #(.width(32)) register_21 (.D(WriteData), .en(WE17), .clk(Clock), .Q(W17));  // open: clr
  Register #(.width(32)) register_22 (.D(WriteData), .en(WE21), .clk(Clock), .Q(W21));  // open: clr
  Register #(.width(32)) register_23 (.D(WriteData), .en(WE25), .clk(Clock), .Q(W25));  // open: clr
  Register #(.width(32)) register_24 (.D(WriteData), .en(WE29), .clk(Clock), .Q(W29));  // open: clr
  Register #(.width(32)) register_25 (.D(WriteData), .en(WE2), .clk(Clock), .Q(W2));  // open: clr
  Register #(.width(32)) register_26 (.D(WriteData), .en(WE6), .clk(Clock), .Q(W6));  // open: clr
  Register #(.width(32)) register_27 (.D(WriteData), .en(WE10), .clk(Clock), .Q(W10));  // open: clr
  Register #(.width(32)) register_28 (.D(WriteData), .en(WE14), .clk(Clock), .Q(W14));  // open: clr
  Register #(.width(32)) register_29 (.D(WriteData), .en(WE18), .clk(Clock), .Q(W18));  // open: clr
  Register #(.width(32)) register_30 (.D(WriteData), .en(WE22), .clk(Clock), .Q(W22));  // open: clr
  Register #(.width(32)) register_31 (.D(WriteData), .en(WE26), .clk(Clock), .Q(W26));  // open: clr
  Register #(.width(32)) register_32 (.D(WriteData), .en(WE30), .clk(Clock), .Q(W30));  // open: clr
  Register #(.width(32)) register_33 (.D(WriteData), .en(WE3), .clk(Clock), .Q(W3));  // open: clr
  Register #(.width(32)) register_34 (.D(WriteData), .en(WE7), .clk(Clock), .Q(W7));  // open: clr
  Register #(.width(32)) register_35 (.D(WriteData), .en(WE11), .clk(Clock), .Q(W11));  // open: clr
  Register #(.width(32)) register_36 (.D(WriteData), .en(WE15), .clk(Clock), .Q(W15));  // open: clr
  Register #(.width(32)) register_37 (.D(WriteData), .en(WE19), .clk(Clock), .Q(W19));  // open: clr
  Register #(.width(32)) register_38 (.D(WriteData), .en(WE23), .clk(Clock), .Q(W23));  // open: clr
  Register #(.width(32)) register_39 (.D(WriteData), .en(WE27), .clk(Clock), .Q(W27));  // open: clr
  Register #(.width(32)) register_40 (.D(WriteData), .en(WE31), .clk(Clock), .Q(W31));  // open: clr
  Multiplexer #(.select(2), .width(32)) multiplexer_1 (
    .in0(W0), .in1(W1), .in2(W2), .in3(W3), .out(multiplexer_1_out), .sel(Address[3:2]));
  Multiplexer #(.select(2), .width(32)) multiplexer_2 (
    .in0(W4), .in1(W5), .in2(W6), .in3(W7), .out(multiplexer_2_out), .sel(Address[3:2]));
  Multiplexer #(.select(2), .width(32)) multiplexer_3 (
    .in0(W8), .in1(W9), .in2(W10), .in3(W11), .out(multiplexer_3_out), .sel(Address[3:2]));
  Multiplexer #(.select(2), .width(32)) multiplexer_4 (
    .in0(W12), .in1(W13), .in2(W14), .in3(W15), .out(multiplexer_4_out), .sel(Address[3:2]));
  Multiplexer #(.select(2), .width(32)) multiplexer_5 (
    .in0(W16), .in1(W17), .in2(W18), .in3(W19), .out(multiplexer_5_out), .sel(Address[3:2]));
  Multiplexer #(.select(2), .width(32)) multiplexer_6 (
    .in0(W20), .in1(W21), .in2(W22), .in3(W23), .out(multiplexer_6_out), .sel(Address[3:2]));
  Multiplexer #(.select(2), .width(32)) multiplexer_7 (
    .in0(W24), .in1(W25), .in2(W26), .in3(W27), .out(multiplexer_7_out), .sel(Address[3:2]));
  Multiplexer #(.select(2), .width(32)) multiplexer_8 (
    .in0(W28), .in1(W29), .in2(W30), .in3(W31), .out(multiplexer_8_out), .sel(Address[3:2]));
  Multiplexer #(.width(32)) multiplexer_9 (
    .in0(multiplexer_1_out), .in1(multiplexer_2_out), .out(multiplexer_9_out), .sel(Select_0));
  Multiplexer #(.width(32)) multiplexer_10 (
    .in0(multiplexer_3_out), .in1(multiplexer_4_out), .out(multiplexer_10_out), .sel(Select_1));
  Multiplexer #(.width(32)) multiplexer_11 (
    .in0(multiplexer_5_out), .in1(multiplexer_6_out), .out(multiplexer_11_out), .sel(Select_2));
  Multiplexer #(.width(32)) multiplexer_12 (
    .in0(multiplexer_7_out), .in1(multiplexer_8_out), .out(multiplexer_12_out), .sel(Select_3));
  Multiplexer #(.select(2), .width(32)) multiplexer_13 (
    .in0(multiplexer_9_out), .in1(multiplexer_10_out), .in2(multiplexer_11_out), .in3(multiplexer_12_out),
    .out(ReadData), .sel(Address[5:4]));
  Comparator #(.width(10)) comparator_1 (.a(B1[9:0]), .b(Address[15:6]), .eq(Select_0));  // open: gt, lt
  Comparator #(.width(10)) comparator_2 (.a(B0[9:0]), .b(Address[15:6]), .eq(comparator_2_eq));  // open: gt, lt
  and and_1 (and_1_out, B1[10], Select_0);
  and and_2 (and_2_out, B0[10], comparator_2_eq);
  or or_1 (or_1_out, and_1_out, and_2_out);
  Comparator #(.width(10)) comparator_3 (.a(B3[9:0]), .b(Address[15:6]), .eq(Select_1));  // open: gt, lt
  Comparator #(.width(10)) comparator_4 (.a(B2[9:0]), .b(Address[15:6]), .eq(comparator_4_eq));  // open: gt, lt
  and and_3 (and_3_out, B3[10], Select_1);
  and and_4 (and_4_out, B2[10], comparator_4_eq);
  Multiplexer #(.select(2)) multiplexer_14 (
    .in0(or_1_out), .in1(or_2_out), .in2(or_3_out), .in3(or_4_out), .out(HIT), .sel(Address[5:4]));
  or or_2 (or_2_out, and_3_out, and_4_out);
  and and_5 (and_5_out, ~Select_0, Set0, WH);  // AND_Gate
  and and_6 (and_6_out, Select_0, Set0, WH);
  and and_7 (and_7_out, ~Select_1, Set1, WH);  // AND_Gate
  and and_8 (and_8_out, Select_1, Set1, WH);
  and and_9 (and_9_out, ~Select_2, Set2, WH);  // AND_Gate
  and and_10 (and_10_out, Select_2, Set2, WH);
  and and_11 (and_11_out, ~Select_3, Set3, WH);  // AND_Gate
  and and_12 (and_12_out, Select_3, Set3, WH);
  Comparator #(.width(10)) comparator_5 (.a(B5[9:0]), .b(Address[15:6]), .eq(Select_2));  // open: gt, lt
  Comparator #(.width(10)) comparator_6 (.a(B4[9:0]), .b(Address[15:6]), .eq(comparator_6_eq));  // open: gt, lt
  and and_13 (WH, in_4, HIT);
  and and_14 (WE0, Word0, and_5_out);
  and and_15 (WE4, Word0, and_6_out);
  and and_16 (WE8, Word0, and_7_out);
  and and_17 (WE12, Word0, and_8_out);
  and and_18 (WE16, Word0, and_9_out);
  and and_19 (WE20, Word0, and_10_out);
  and and_20 (WE24, Word0, and_11_out);
  and and_21 (WE28, Word0, and_12_out);
  and and_22 (and_22_out, B5[10], Select_2);
  or or_3 (or_3_out, and_22_out, and_23_out);
  and and_23 (and_23_out, B4[10], comparator_6_eq);
  and and_24 (WE1, Word1, and_5_out);
  and and_25 (WE5, Word1, and_6_out);
  and and_26 (WE9, Word1, and_7_out);
  and and_27 (WE13, Word1, and_8_out);
  and and_28 (WE17, Word1, and_9_out);
  and and_29 (WE21, Word1, and_10_out);
  and and_30 (WE25, Word1, and_11_out);
  and and_31 (WE29, Word1, and_12_out);
  Comparator #(.width(10)) comparator_7 (.a(B7[9:0]), .b(Address[15:6]), .eq(Select_3));  // open: gt, lt
  Comparator #(.width(10)) comparator_8 (.a(B6[9:0]), .b(Address[15:6]), .eq(comparator_8_eq));  // open: gt, lt
  and and_32 (and_32_out, B7[10], Select_3);
  and and_33 (and_33_out, B6[10], comparator_8_eq);
  and and_34 (WE2, Word2, and_5_out);
  and and_35 (WE6, Word2, and_6_out);
  and and_36 (WE10, Word2, and_7_out);
  and and_37 (WE14, Word2, and_8_out);
  and and_38 (WE18, Word2, and_9_out);
  and and_39 (WE22, Word2, and_10_out);
  and and_40 (WE26, Word2, and_11_out);
  and and_41 (WE30, Word2, and_12_out);
  or or_4 (or_4_out, and_32_out, and_33_out);
  and and_42 (WE3, Word3, and_5_out);
  and and_43 (WE7, Word3, and_6_out);
  and and_44 (WE11, Word3, and_7_out);
  and and_45 (WE15, Word3, and_8_out);
  and and_46 (WE19, Word3, and_9_out);
  and and_47 (WE23, Word3, and_10_out);
  and and_48 (WE27, Word3, and_11_out);
  and and_49 (WE31, Word3, and_12_out);

  assign AddressOut = Address;

  // Other names for the same wires on the sheet: word[1:0] = Address[3:2]; Set[1:0] = Address[5:4];
  //   Tag[9:0] = Address[15:6]; WE = in_4
endmodule
