// Logisim project cpu.circ as structural Verilog: 1 circuit, main circuit cpu
module cpu (
  input  Reset
);

  wire alucontroller_1_sh_amount, aluZero, and_1_out, and_2_out, and_3_out, and_6_out, AO, BR, BR_EXMEM,
       branch_detector_1_branch, branch_detector_1_jump, cache_1_readfrommem, cache_1_writeinmemory, clk,
       comparator_1_eq, comparator_2_eq, comparator_3_eq, controller_1_alusrc, controller_1_branch,
       controller_1_jump, controller_1_lb, controller_1_memtoreg, controller_1_regdst, controller_1_regwren,
       ex_mem_1_memtoregout, ex_mem_1_regdstout, ex_mem_1_regwrenout, id_ex_1_p23, id_ex_1_p33, JO, JR_EXMEM,
       JR_WB, Jump_EXMEM, Jump_WB, LB, memToReg, MTR, multiplexer_2_out, not_1_out, or_1_out, or_2_out,
       Prediction, RD, RegDst_WB, regfile_1_p7, regfile_1_p8, RegWrEn_WB, rst, RType, RType2, RW, select_pc,
       Syscall_EXMEM, Syscall_WB, wrongPrediction, Zero_EXMEM;
  wire [1:0] alu_1_result, undriven;
  wire [3:0] bit_extender_5_out, controller_1_memwrmask, ex_mem_1_memwritemaskout, id_ex_1_p26,
       multiplexer_11_out, oneclockdelay_1_dataout_2, shifter_4_out;
  wire [4:0] alucontroller_1_alu_out, bit_extender_4_out, ex_mem_1_wridxout, id_ex_1_p32, multiplexer_7_out,
       shifter_5_out, WrIdx, WrIdx_IDEX, WrIdx_WB;
  wire [7:0] multiplexer_16_out;
  wire [25:0] oneclockdelay_2_dataout;
  wire [27:0] oneclockdelay_1_dataout;
  wire [31:0] adder_1_out, adder_2_out, AluRes_EXMEM, AluRes_WB, bit_extender_1_out, bit_extender_2_out,
       bit_extender_3_out, bit_extender_6_out, cache_1_readdata, cache_1_writeaddressout,
       cache_1_writedataout, ex_mem_1_addresscacheout, ex_mem_pc_1_br_pcout, ex_mem_pc_1_j_pcout,
       ex_mem_pc_1_pcout, id_ex_1_p28, id_ex_1_p29, id_ex_1_p30, id_ex_1_p31, id_ex_pc_1_j_pcout,
       id_ex_pc_1_pcout, mem_1_memreaddata, mem_wb_1_cachereadout, MemData, multiplexer_1_out,
       multiplexer_3_out, multiplexer_4_out, multiplexer_5_out, multiplexer_8_out, multiplexer_9_out,
       multiplexer_10_out, multiplexer_12_out, multiplexer_13_out, multiplexer_14_out, multiplexer_17_out,
       multiplexer_18_out, pc_4_d, pc_branch, pc_branch_d, PC_EXMEM, PC_q, PC_WB, shifter_1_out,
       shifter_2_out, shifter_3_out, shifter_6_out, signextend_1_extended, undriven_2, xor_1_out;
  wire [31:2] alu_1_result_2;
  wire [31:26] oneclockdelay_2_dataout_2;

  Multiplexer #(.width(32)) multiplexer_1 (
    .in0(multiplexer_3_out), .in1(AluRes_WB), .out(multiplexer_1_out), .sel(JR_WB));
  Multiplexer multiplexer_2 (.in0(1'b1), .in1(1'b0), .out(multiplexer_2_out), .sel(Syscall_WB));
  Clock u_Clk (.out(clk));
  Register #(.width(32)) PC (.D(multiplexer_1_out), .en(multiplexer_2_out), .clk(clk), .Q(PC_q), .clr(Reset));
  Multiplexer #(.width(32)) multiplexer_3 (
    .in0(multiplexer_5_out), .in1(multiplexer_4_out), .out(multiplexer_3_out), .sel(wrongPrediction));
  Adder #(.width(32)) adder_1 (.a(32'h4), .b(PC_q), .out(adder_1_out));  // open: cin, cout
  mem mem_1 (.MemAddress(PC_q), .clk(clk), .MemReadData(mem_1_memreaddata));  // open: MemWriteMask, MemWriteData
  branch_detector branch_detector_1 (
    .clk(clk), .rst(rst), .command(mem_1_memreaddata), .pc(PC_q), .pc_branch(pc_branch),
    .Branch(branch_detector_1_branch), .pc_branch_delayed(pc_branch_d), .Jump(branch_detector_1_jump),
    .pc_4_delayed(pc_4_d));
  Multiplexer #(.width(32)) multiplexer_4 (.in0(pc_4_d), .in1(pc_branch_d), .out(multiplexer_4_out), .sel(select_pc));
  Multiplexer #(.width(32)) multiplexer_5 (
    .in0(adder_1_out), .in1(pc_branch), .out(multiplexer_5_out), .sel(Prediction));
  or or_1 (or_1_out, Jump_EXMEM, and_1_out);
  oneClockDelay oneclockdelay_1 (
    .DataIn(adder_1_out), .clk(clk), .reset(rst),
    .DataOut({oneclockdelay_1_dataout_2, oneclockdelay_1_dataout}));
  branchPredictor branchpredictor_1 (
    .Jump(branch_detector_1_jump), .Branch(branch_detector_1_branch), .Clock(clk), .Zero(aluZero),
    .rst_cnt(Reset), .Prediction(Prediction), .wrongPrediction(wrongPrediction), .pcBranch(select_pc),
    .reset(rst));
  oneClockDelay oneclockdelay_2 (
    .DataIn(mem_1_memreaddata), .clk(clk), .reset(rst),
    .DataOut({oneclockdelay_2_dataout_2, oneclockdelay_2_dataout}));
  and and_1 (and_1_out, BR_EXMEM, Zero_EXMEM);
  Multiplexer #(.width(5)) multiplexer_6 (
    .in0(oneclockdelay_2_dataout[20:16]), .in1(oneclockdelay_2_dataout[15:11]), .out(WrIdx),
    .sel(controller_1_regdst));
  assign bit_extender_1_out = {{6{1'b0}}, oneclockdelay_2_dataout};  // Bit_Extender bit_extender_1
  and and_2 (and_2_out, Jump_WB, RegWrEn_WB);
  Multiplexer #(.width(5)) multiplexer_7 (.in0(WrIdx_WB), .in1({5{1'b1}}), .out(multiplexer_7_out), .sel(and_2_out));
  Multiplexer #(.width(32)) multiplexer_8 (
    .in0(multiplexer_18_out), .in1(PC_WB), .out(multiplexer_8_out), .sel(and_2_out));
  Shifter #(.width(32)) shifter_1 (.in(bit_extender_1_out), .\dist (5'b00010), .out(shifter_1_out));
  assign bit_extender_2_out = {{28{1'b0}}, oneclockdelay_1_dataout_2};  // Bit_Extender bit_extender_2
  assign bit_extender_3_out = {{27{1'b0}}, oneclockdelay_2_dataout[10:6]};  // Bit_Extender bit_extender_3
  Shifter #(.width(32)) shifter_2 (.in(bit_extender_2_out), .\dist (5'b11100), .out(shifter_2_out));
  Controller controller_1 (
    .Opcode(oneclockdelay_2_dataout_2), .RegDst(controller_1_regdst), .Branch(controller_1_branch),
    .Jump(controller_1_jump), .RegWrEn(controller_1_regwren), .AluSrc(controller_1_alusrc),
    .MemToReg(controller_1_memtoreg), .AluOpr(AO), .MemWrMask(controller_1_memwrmask), .LB(controller_1_lb));
  assign xor_1_out = shifter_1_out ^ shifter_2_out;  // XOR_Gate xor_1, 32 bits wide
  // regfile regfile_1: pin names not known; wires that end beside it: oneclockdelay_2_dataout[25:21], oneclockdelay_2_dataout[20:16], multiplexer_7_out, multiplexer_8_out, RegWrEn_WB, clk, regfile_1_p7, regfile_1_p8
  signExtend signextend_1 (.Immd(oneclockdelay_2_dataout[15:0]), .Extended(signextend_1_extended));
  AluController alucontroller_1 (
    .func(oneclockdelay_2_dataout[5:0]), .opcode(oneclockdelay_2_dataout_2), .aluOperation(AO),
    .ALU_out(alucontroller_1_alu_out), .sh_amount(alucontroller_1_sh_amount));
  ID_EX_PC id_ex_pc_1 (
    .Clock(clk), .J_PCIN(xor_1_out), .PCIn({oneclockdelay_1_dataout_2, oneclockdelay_1_dataout}),
    .reset(rst), .J_PCOUT(id_ex_pc_1_j_pcout), .PCOut(id_ex_pc_1_pcout));
  // ID_EX id_ex_1: pin names not known; wires that end beside it: clk, controller_1_regdst, controller_1_branch, controller_1_jump, controller_1_regwren, controller_1_alusrc, controller_1_memtoreg, AO, controller_1_memwrmask, controller_1_lb, regfile_1_p7, regfile_1_p8, bit_extender_3_out, signextend_1_extended, alucontroller_1_alu_out, alucontroller_1_sh_amount, WrIdx, rst, RD, BR, JO, RW, id_ex_1_p23, MTR, RType, id_ex_1_p26, LB, id_ex_1_p28, id_ex_1_p29, id_ex_1_p30, id_ex_1_p31, id_ex_1_p32, id_ex_1_p33, WrIdx_IDEX
  and and_3 (and_3_out, ~BR, id_ex_1_p23);  // AND_Gate
  Multiplexer #(.width(32)) multiplexer_9 (
    .in0(id_ex_1_p28), .in1(id_ex_1_p30), .out(multiplexer_9_out), .sel(id_ex_1_p33));
  Shifter #(.width(32)) shifter_3 (.in(id_ex_1_p31), .\dist (5'b00010), .out(shifter_3_out));
  Multiplexer #(.width(32)) multiplexer_10 (
    .in0(id_ex_1_p29), .in1(id_ex_1_p31), .out(multiplexer_10_out), .sel(and_3_out));
  assign bit_extender_4_out = {{3{1'b0}}, alu_1_result};  // Bit_Extender bit_extender_4
  Adder #(.width(32)) adder_2 (.a(id_ex_pc_1_pcout), .b(shifter_3_out), .out(adder_2_out));  // open: cin, cout
  Comparator #(.width(4)) comparator_1 (.a(id_ex_1_p26), .b(4'b0001), .eq(comparator_1_eq));  // open: gt, lt
  Shifter #(.width(4)) shifter_4 (.in(id_ex_1_p26), .\dist (alu_1_result), .out(shifter_4_out));
  Shifter #(.width(5)) shifter_5 (.in(bit_extender_4_out), .\dist (3'b011), .out(shifter_5_out));
  Multiplexer #(.width(4)) multiplexer_11 (
    .in0(id_ex_1_p26), .in1(shifter_4_out), .out(multiplexer_11_out), .sel(comparator_1_eq));
  Shifter #(.width(32)) shifter_6 (.in(id_ex_1_p29), .\dist (shifter_5_out), .out(shifter_6_out));
  ALU alu_1 (
    .ReadData1(multiplexer_9_out), .ReadData2(multiplexer_10_out), .ControlBits(id_ex_1_p32),
    .Result({alu_1_result_2, alu_1_result}), .Zero(aluZero));
  Multiplexer #(.width(32)) multiplexer_12 (
    .in0(id_ex_1_p29), .in1(shifter_6_out), .out(multiplexer_12_out), .sel(comparator_1_eq));
  EX_MEM_PC ex_mem_pc_1 (
    .Clock(clk), .J_PCIN(id_ex_pc_1_j_pcout), .PCIN(id_ex_pc_1_pcout), .BR_PCIN(adder_2_out),
    .J_PCOUT(ex_mem_pc_1_j_pcout), .PCOUT(ex_mem_pc_1_pcout), .BR_PCOUT(ex_mem_pc_1_br_pcout));
  EX_MEM ex_mem_1 (
    .Clock(clk), .ResultIn({alu_1_result_2, alu_1_result}), .AddressCacheIn(multiplexer_12_out),
    .ZeroIn(aluZero), .BranchIn(BR), .RtypeIn(RType), .JumpIn(JO), .MemToRegIn(MTR), .RegDstIn(RD),
    .RegWrEnIn(RW), .MemWriteMaskIn(multiplexer_11_out), .LBIn(LB), .WrIdxIn(WrIdx_IDEX),
    .ResultOut(AluRes_EXMEM), .AddressCacheOut(ex_mem_1_addresscacheout), .ZeroOut(Zero_EXMEM),
    .BranchOut(BR_EXMEM), .RtypeOut(RType2), .JumpOut(Jump_EXMEM), .MemToRegOut(ex_mem_1_memtoregout),
    .RegDstOut(ex_mem_1_regdstout), .RegWrEnOut(ex_mem_1_regwrenout),
    .MemWriteMaskOut(ex_mem_1_memwritemaskout), .WrIdxOut(ex_mem_1_wridxout));  // open: Freeze, LBOut
  and and_4 (Syscall_EXMEM, RType2, Zero_EXMEM, comparator_3_eq);
  and and_5 (JR_EXMEM, Zero_EXMEM, ~comparator_3_eq, RType2);  // AND_Gate
  Multiplexer #(.width(32)) multiplexer_13 (.in0(MemData), .in1(AluRes_EXMEM), .out(multiplexer_13_out));  // open: sel
  Comparator #(.width(4)) comparator_2 (
    .a(4'b1111), .b(ex_mem_1_memwritemaskout), .eq(comparator_2_eq));  // open: gt, lt
  Multiplexer #(.width(32)) multiplexer_14 (
    .in0(ex_mem_pc_1_pcout), .in1(ex_mem_pc_1_br_pcout), .out(multiplexer_14_out), .sel(and_6_out));
  not not_1 (not_1_out, Jump_EXMEM);
  and and_6 (and_6_out, BR_EXMEM, Zero_EXMEM);
  or or_2 (or_2_out, cache_1_readfrommem, comparator_2_eq);
  assign bit_extender_5_out = {{3{cache_1_writeinmemory}}, cache_1_writeinmemory};  // Bit_Extender bit_extender_5
  Multiplexer #(.width(32)) multiplexer_15 (
    .in0(ex_mem_pc_1_j_pcout), .in1(multiplexer_14_out), .out(PC_EXMEM), .sel(not_1_out));
  Comparator #(.width(32)) comparator_3 (.a(AluRes_EXMEM), .b({32{1'b1}}), .eq(comparator_3_eq));  // open: gt, lt
  Cache cache_1 (
    .clk(clk), .Address(ex_mem_1_addresscacheout), .WriteEnable(or_2_out), .WriteData(multiplexer_13_out),
    .ReadFromMem(cache_1_readfrommem), .ReadData(cache_1_readdata),
    .WriteAddressOut(cache_1_writeaddressout), .WriteInMemory(cache_1_writeinmemory),
    .WriteDataOut(cache_1_writedataout));  // open: HIT, ReadAddressOut
  memDelayed memdelayed_1 (
    .MemAddress(cache_1_writeaddressout), .MemWriteMask(bit_extender_5_out),
    .MemWriteData(cache_1_writedataout), .clk(clk), .MemReadData(MemData));
  MEM_WB mem_wb_1 (
    .Clock(clk), .CacheReadDataIn(cache_1_readdata), .MemToRegIn(ex_mem_1_memtoregout), .JumpIn(Jump_EXMEM),
    .RegDstIn(ex_mem_1_regdstout), .RegWrEnIn(ex_mem_1_regwrenout), .ALU_RES(AluRes_EXMEM),
    .WrIdxIn(ex_mem_1_wridxout), .PCIN(PC_EXMEM), .SyscalIN(Syscall_EXMEM), .JRIN(JR_EXMEM), .FRZ(JR_EXMEM),
    .CacheReadOut(mem_wb_1_cachereadout), .MemToRegOut(memToReg), .JumpOut(Jump_WB), .RegDstOut(RegDst_WB),
    .RegWrEnOut(RegWrEn_WB), .AluRes_WB(AluRes_WB), .WrIdxOut(WrIdx_WB), .PCOUT(PC_WB),
    .SyscallOut(Syscall_WB), .JROUT(JR_WB));
  assign bit_extender_6_out = {{24{1'b1}}, multiplexer_16_out};  // Bit_Extender bit_extender_6
  Multiplexer #(.select(2), .width(8)) multiplexer_16 (
    .in0(undriven_2[7:0]), .in1(undriven_2[15:8]), .in2(undriven_2[23:16]), .in3(undriven_2[31:24]),
    .out(multiplexer_16_out), .sel(undriven));
  Multiplexer #(.width(32)) multiplexer_17 (
    .in0(undriven_2), .in1(bit_extender_6_out), .out(multiplexer_17_out), .sel(LB));
  Multiplexer #(.width(32)) multiplexer_18 (
    .in0(AluRes_WB), .in1(mem_wb_1_cachereadout), .out(multiplexer_18_out), .sel(memToReg));

  // Other names for the same wires on the sheet: pcReset = Reset
endmodule
