// Logisim project one_clock_delay.circ as structural Verilog: 1 circuit, main circuit oneClockDelay
module oneClockDelay (
  input  [31:0] DataIn,
  input  clk,
  input  reset,
  output [31:0] DataOut
);

  Register #(.width(32)) register_1 (.D(DataIn), .clk(clk), .Q(DataOut), .clr(reset));  // open: en
endmodule
